// Logisim project Мирик4D8421.circ as structural Verilog: 1 circuit, main circuit main
module main (
  input  [3:0] in_1,
  output [3:0] out_2
);

  wire and_1_out, and_2_out, and_3_out, not_1_out, not_2_out, not_3_out, not_4_out, not_5_out, not_6_out,
       or_1_out;

  and and_1 (and_1_out, in_1[3], in_1[2]);
  and and_2 (and_2_out, in_1[3], in_1[1]);
  not not_1 (not_1_out, in_1[0]);
  not not_2 (not_2_out, in_1[1]);
  and and_3 (and_3_out, not_2_out, not_3_out);
  not not_3 (not_3_out, in_1[2]);
  not not_4 (not_4_out, in_1[3]);
  and and_4 (out_2[3], not_1_out, and_3_out, not_4_out);
  or or_1 (or_1_out, and_1_out, and_2_out);
  not not_5 (not_5_out, in_1[3]);
  and and_5 (out_2[2], or_1_out, not_5_out);
  // Probe on or_1_out
  LED led_1 (.in(or_1_out));
  not not_6 (not_6_out, or_1_out);
  LED led_2 (.in(not_6_out));

  assign out_2[1:0] = {out_2[2], out_2[3]};
endmodule
