// Logisim project Мириклаб5.circ as structural Verilog: 1 circuit, main circuit main
module main (
  input  in_1,
  input  in_2,
  input  in_3,
  input  in_4,
  output [2:0] out_5
);

  wire and_1_out, and_2_out, button_1_out;

  T_Flip_Flop t_ff_1 ();  // open: clk, T, Q, Qn, preset, reset, en
  and and_1 (and_1_out, and_2_out, out_5[1]);
  and and_2 (and_2_out, in_1, out_5[0]);
  Button button_1 (.out(button_1_out));
  T_Flip_Flop t_ff_2 (
    .clk(button_1_out), .T(and_1_out), .Qn(out_5[2]), .preset(in_2), .reset(in_4), .en(in_3));  // open: Q
  T_Flip_Flop t_ff_3 (
    .clk(button_1_out), .T(and_2_out), .Qn(out_5[1]), .preset(in_2), .reset(in_4), .en(in_3));  // open: Q
  T_Flip_Flop #(.trigger("falling")) t_ff_4 (
    .clk(button_1_out), .T(in_1), .Qn(out_5[0]), .preset(in_2), .reset(in_4), .en(in_3));  // open: Q
endmodule
