// Logisim project SUMMATOR_8bit.circ as structural Verilog: 2 circuits, main circuit main
module main (
  input  [7:0] A,
  input  [7:0] B,
  output [7:0] SUM
);

  wire and_2_out, and_4_out, and_7_out, and_8_out, and_11_out, and_12_out, and_15_out, and_16_out, not_1_out,
       not_2_out, not_3_out, not_4_out, not_5_out, not_6_out, not_7_out, not_8_out, not_9_out, not_10_out,
       not_11_out, not_12_out, not_13_out, not_14_out, not_15_out, not_16_out, not_17_out, not_18_out,
       not_19_out, not_20_out, not_21_out, not_22_out, not_23_out, not_24_out, or_1_out, or_2_out, or_3_out,
       or_4_out, or_5_out, or_6_out, or_7_out, or_8_out, or_9_out, or_10_out, or_11_out, or_12_out,
       or_13_out, or_14_out, or_15_out, or_16_out, or_17_out, or_18_out, or_19_out, or_20_out, or_21_out,
       or_22_out, or_23_out, or_24_out, or_25_out, or_26_out, or_27_out, or_28_out, or_29_out, or_30_out,
       or_31_out, or_32_out, or_33_out, or_34_out, or_35_out, or_36_out, or_37_out, or_38_out, or_39_out,
       or_40_out, or_41_out, or_42_out, or_43_out, or_44_out, or_45_out, or_46_out, or_47_out, or_48_out,
       or_49_out, or_50_out, or_51_out, or_52_out, or_53_out, or_54_out, or_55_out, or_56_out;

  // Probe on B
  // Probe on SUM
  LED OVERFLOW (.in(and_15_out));
  // Probe on A
  not not_1 (not_1_out, A[0]);
  not not_2 (not_2_out, B[0]);
  not not_3 (not_3_out, 1'b0);
  not not_4 (not_4_out, A[4]);
  not not_5 (not_5_out, B[4]);
  not not_6 (not_6_out, and_16_out);
  or or_1 (or_1_out, A[0], not_2_out, not_3_out);
  or or_2 (or_2_out, not_1_out, B[0], not_3_out);
  or or_3 (or_3_out, not_1_out, not_2_out, 1'b0);
  or or_4 (or_4_out, A[0], B[0], 1'b0);
  and and_1 (SUM[0], or_1_out, or_2_out, or_3_out, or_4_out);
  or or_5 (or_5_out, A[0], 1'b0);
  or or_6 (or_6_out, A[0], B[0]);
  or or_7 (or_7_out, B[0], 1'b0);
  or or_8 (or_8_out, A[4], not_5_out, not_6_out);
  or or_9 (or_9_out, not_4_out, B[4], not_6_out);
  or or_10 (or_10_out, not_4_out, not_5_out, and_16_out);
  or or_11 (or_11_out, A[4], B[4], and_16_out);
  and and_2 (and_2_out, or_5_out, or_6_out, or_7_out);
  and and_3 (SUM[4], or_8_out, or_9_out, or_10_out, or_11_out);
  or or_12 (or_12_out, A[4], and_16_out);
  or or_13 (or_13_out, A[4], B[4]);
  or or_14 (or_14_out, B[4], and_16_out);
  and and_4 (and_4_out, or_12_out, or_13_out, or_14_out);
  not not_7 (not_7_out, A[1]);
  not not_8 (not_8_out, B[1]);
  not not_9 (not_9_out, and_2_out);
  not not_10 (not_10_out, A[5]);
  not not_11 (not_11_out, B[5]);
  not not_12 (not_12_out, and_4_out);
  or or_15 (or_15_out, A[1], not_8_out, not_9_out);
  or or_16 (or_16_out, not_7_out, B[1], not_9_out);
  or or_17 (or_17_out, not_7_out, not_8_out, and_2_out);
  or or_18 (or_18_out, A[1], B[1], and_2_out);
  and and_5 (SUM[1], or_15_out, or_16_out, or_17_out, or_18_out);
  or or_19 (or_19_out, A[5], not_11_out, not_12_out);
  or or_20 (or_20_out, not_10_out, B[5], not_12_out);
  or or_21 (or_21_out, not_10_out, not_11_out, and_4_out);
  or or_22 (or_22_out, A[5], B[5], and_4_out);
  or or_23 (or_23_out, A[1], and_2_out);
  or or_24 (or_24_out, A[1], B[1]);
  or or_25 (or_25_out, B[1], and_2_out);
  and and_6 (SUM[5], or_19_out, or_20_out, or_21_out, or_22_out);
  or or_26 (or_26_out, A[5], and_4_out);
  or or_27 (or_27_out, A[5], B[5]);
  or or_28 (or_28_out, B[5], and_4_out);
  and and_7 (and_7_out, or_23_out, or_24_out, or_25_out);
  and and_8 (and_8_out, or_26_out, or_27_out, or_28_out);
  not not_13 (not_13_out, A[6]);
  not not_14 (not_14_out, B[6]);
  not not_15 (not_15_out, and_8_out);
  not not_16 (not_16_out, A[2]);
  not not_17 (not_17_out, B[2]);
  not not_18 (not_18_out, and_7_out);
  or or_29 (or_29_out, A[6], not_14_out, not_15_out);
  or or_30 (or_30_out, not_13_out, B[6], not_15_out);
  or or_31 (or_31_out, not_13_out, not_14_out, and_8_out);
  or or_32 (or_32_out, A[6], B[6], and_8_out);
  or or_33 (or_33_out, A[2], not_17_out, not_18_out);
  or or_34 (or_34_out, not_16_out, B[2], not_18_out);
  or or_35 (or_35_out, not_16_out, not_17_out, and_7_out);
  or or_36 (or_36_out, A[2], B[2], and_7_out);
  and and_9 (SUM[2], or_33_out, or_34_out, or_35_out, or_36_out);
  and and_10 (SUM[6], or_29_out, or_30_out, or_31_out, or_32_out);
  or or_37 (or_37_out, A[6], and_8_out);
  or or_38 (or_38_out, A[6], B[6]);
  or or_39 (or_39_out, B[6], and_8_out);
  or or_40 (or_40_out, A[2], and_7_out);
  or or_41 (or_41_out, A[2], B[2]);
  or or_42 (or_42_out, B[2], and_7_out);
  and and_11 (and_11_out, or_37_out, or_38_out, or_39_out);
  and and_12 (and_12_out, or_40_out, or_41_out, or_42_out);
  not not_19 (not_19_out, A[7]);
  not not_20 (not_20_out, B[7]);
  not not_21 (not_21_out, and_11_out);
  not not_22 (not_22_out, A[3]);
  not not_23 (not_23_out, B[3]);
  not not_24 (not_24_out, and_12_out);
  or or_43 (or_43_out, A[7], not_20_out, not_21_out);
  or or_44 (or_44_out, not_19_out, B[7], not_21_out);
  or or_45 (or_45_out, not_19_out, not_20_out, and_11_out);
  or or_46 (or_46_out, A[7], B[7], and_11_out);
  or or_47 (or_47_out, A[3], not_23_out, not_24_out);
  or or_48 (or_48_out, not_22_out, B[3], not_24_out);
  or or_49 (or_49_out, not_22_out, not_23_out, and_12_out);
  or or_50 (or_50_out, A[3], B[3], and_12_out);
  and and_13 (SUM[7], or_43_out, or_44_out, or_45_out, or_46_out);
  or or_51 (or_51_out, A[7], and_11_out);
  or or_52 (or_52_out, A[7], B[7]);
  or or_53 (or_53_out, B[7], and_11_out);
  and and_14 (SUM[3], or_47_out, or_48_out, or_49_out, or_50_out);
  or or_54 (or_54_out, A[3], and_12_out);
  or or_55 (or_55_out, A[3], B[3]);
  or or_56 (or_56_out, B[3], and_12_out);
  and and_15 (and_15_out, or_51_out, or_52_out, or_53_out);
  and and_16 (and_16_out, or_54_out, or_55_out, or_56_out);
endmodule

module main_f (
  input  [7:0] in_1,
  input  [7:0] in_2,
  output [7:0] out_3
);

  wire main_1_p3, main_1_p5, main_2_p6, main_3_p6, main_4_p6, main_5_p6, main_6_p6, main_7_p6;

  // Probe on in_1
  // Probe on in_2
  // main main_1: pin names not known; wires that end beside it: in_1[0], in_2[0], main_1_p3, in_1[1], main_1_p5, out_3[0]
  // main main_2: pin names not known; wires that end beside it: main_1_p3, in_1[1], in_2[1], main_1_p5, in_1[2], main_2_p6, out_3[1]
  // main main_3: pin names not known; wires that end beside it: main_1_p5, in_1[2], in_2[2], main_2_p6, in_1[3], main_3_p6, out_3[2]
  // main main_4: pin names not known; wires that end beside it: main_2_p6, in_1[3], in_2[3], main_3_p6, in_1[4], main_4_p6, out_3[3]
  // main main_5: pin names not known; wires that end beside it: main_3_p6, in_1[4], in_2[4], main_4_p6, in_1[5], main_5_p6, out_3[4]
  // main main_6: pin names not known; wires that end beside it: main_4_p6, in_1[5], in_2[5], main_5_p6, in_1[6], main_6_p6, out_3[5]
  // main main_7: pin names not known; wires that end beside it: main_5_p6, in_1[6], in_2[6], main_6_p6, in_1[7], main_7_p6, out_3[6]
  // main main_8: pin names not known; wires that end beside it: main_6_p6, in_1[7], in_2[7], main_7_p6, main_1_p3, out_3[7]
  // Probe on out_3
endmodule
