// Logisim project Мириклаб5.circ as structural Verilog: 1 circuit, main circuit main
module main (
  input  in_1,
  input  in_2,
  input  in_3,
  input  in_4,
  output [7:0] out_5
);

  wire and_1_out, and_2_out, and_3_out, and_4_out, and_5_out, and_6_out, and_7_out, button_1_out;

  T_Flip_Flop t_ff_1 ();  // open: clk, T, Q, Qn, preset, reset, en
  and and_1 (and_1_out, and_2_out, out_5[6]);
  and and_2 (and_2_out, and_3_out, out_5[5]);
  and and_3 (and_3_out, and_4_out, out_5[4]);
  and and_4 (and_4_out, and_5_out, out_5[3]);
  and and_5 (and_5_out, and_6_out, out_5[2]);
  and and_6 (and_6_out, and_7_out, out_5[1]);
  and and_7 (and_7_out, in_1, out_5[0]);
  Button button_1 (.out(button_1_out));
  T_Flip_Flop t_ff_2 (
    .clk(button_1_out), .T(and_1_out), .Qn(out_5[7]), .preset(in_2), .reset(in_4), .en(in_3));  // open: Q
  T_Flip_Flop t_ff_3 (
    .clk(button_1_out), .T(and_2_out), .Qn(out_5[6]), .preset(in_2), .reset(in_4), .en(in_3));  // open: Q
  T_Flip_Flop t_ff_4 (
    .clk(button_1_out), .T(and_3_out), .Qn(out_5[5]), .preset(in_2), .reset(in_4), .en(in_3));  // open: Q
  T_Flip_Flop t_ff_5 (
    .clk(button_1_out), .T(and_4_out), .Qn(out_5[4]), .preset(in_2), .reset(in_4), .en(in_3));  // open: Q
  T_Flip_Flop t_ff_6 (
    .clk(button_1_out), .T(and_5_out), .Qn(out_5[3]), .preset(in_2), .reset(in_4), .en(in_3));  // open: Q
  T_Flip_Flop t_ff_7 (
    .clk(button_1_out), .T(and_6_out), .Qn(out_5[2]), .preset(in_2), .reset(in_4), .en(in_3));  // open: Q
  T_Flip_Flop t_ff_8 (
    .clk(button_1_out), .T(and_7_out), .Qn(out_5[1]), .preset(in_2), .reset(in_4), .en(in_3));  // open: Q
  T_Flip_Flop #(.trigger("falling")) t_ff_9 (
    .clk(button_1_out), .T(in_1), .Qn(out_5[0]), .preset(in_2), .reset(in_4), .en(in_3));  // open: Q
endmodule
